# Fritzing sketch timing Gate v3.0 GND (saved by Fritzing 0.9.6b)
circuit board: 10.0541cm x 6.1393cm
breadboards: 1

parts:
  SG1 = Buzzer 12mm top view [package=buzzer-12mm-ns]
  R1 = Resistor [tolerance=±5% power=0.25 resistance=100 package=THT]
  R2 = Resistor [tolerance=±5% power=0.25 resistance=100 package=THT]
  Adafruit_Feather_M0 = Adafruit Feather M0 Basic Proto [part_number="Adafruit #2772"]
  J2_Left_Gate_LED = male pin header, 2 pins [form="♂ (male)"]
  J1_Power_Enable = double row male pin header, 2 pins [form="♂ (male)"]
  J3_Right_Gate_LED = male pin header, 2 pins [form="♂ (male)"]
  U1_Left_Gate = Sharp PC817 [package=THT]
  R3 = Resistor [tolerance=±5% power=0.25 resistance=1k package=THT]
  U2_Right_Gate = Sharp PC817 [package=THT]
  J4_Right_Gate_Sensor = male pin header, 4 pins [form="♂ (male)"]
  DC-DC_Convertor = IC, SIP package, 3 pins [chip_label=DC-DC]
  R4 = Resistor [tolerance=±5% power=0.25 resistance=1k package=THT]
  J4_LDC_Display = male pin header, 4 pins [form="♂ (male)"]
  J4_Left_Gate_Sensor = male pin header, 4 pins [form="♂ (male)"]

nets (from the schematic view):
  N1: SG1.1, Adafruit_Feather_M0.A3
  GND: SG1.2, Adafruit_Feather_M0.GND, J2_Left_Gate_LED.pin2, J3_Right_Gate_LED.pin2, U1_Left_Gate.Pin_2, U1_Left_Gate.Pin_3, U2_Right_Gate.Pin_2, U2_Right_Gate.Pin_3, J4_Right_Gate_Sensor.pin2, DC-DC_Convertor.pin2, J4_LDC_Display.pin4, J4_Left_Gate_Sensor.pin2
  N2: R1.Pin_0, Adafruit_Feather_M0.D5
  N3: R1.Pin_1, J3_Right_Gate_LED.pin1
  N4: R2.Pin_0, Adafruit_Feather_M0.D6
  N5: R2.Pin_1, J2_Left_Gate_LED.pin1
  5V: Adafruit_Feather_M0.+3V3, DC-DC_Convertor.pin1, J4_LDC_Display.pin3
  N6: Adafruit_Feather_M0.EN, J1_Power_Enable.pin1
  left gate: Adafruit_Feather_M0.D11, U1_Left_Gate.Pin_4
  right Gate: Adafruit_Feather_M0.D10, U2_Right_Gate.Pin_4
  N7: Adafruit_Feather_M0.SCL, J4_LDC_Display.pin1
  N8: Adafruit_Feather_M0.SDA, J4_LDC_Display.pin2
  N9: U1_Left_Gate.Pin_1, J4_Left_Gate_Sensor.pin4
  12V: R3.Pin_0, J4_Right_Gate_Sensor.pin1, DC-DC_Convertor.pin3, R4.Pin_0, J4_Left_Gate_Sensor.pin1
  N10: R3.Pin_1, J4_Left_Gate_Sensor.pin3
  N11: U2_Right_Gate.Pin_1, J4_Right_Gate_Sensor.pin4
  N12: J4_Right_Gate_Sensor.pin3, R4.Pin_1

notes:
  Wired timing gates, v3.0
  +12V
  0V
  sensor white
  sensor black
  SCL
  3.3v
  GND
  SDA
  3V
  12v
  Tc
  Ta
  Vin
  Vout 12v

custom parts:
  Buzzer 12mm top view: Buzzer 12mm
  Adafruit Feather M0 Basic Proto: At the Feather M0's heart is an ATSAMD21G18 ARM Cortex M0 processor, clocked at 48 MHz and at 3.3V logic, the same one used in the new Arduino Zero. This chip has a whopping 256K of FLASH (8x more than the Atmega328 or 32u4) and 32K of RAM (16x as much)! This chip comes with built in USB so it has USB-to-Serial program & debug capability built in with no need for an FTDI-like chip. To make it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

// code stored in the sketch: timing gates.ino
#include <FlashStorage_SAMD.h>
#include <FlashStorage_SAMD21.h>
#include <Arduino.h>
//#include <u8x8lib.h>
#include <EasyButton.h>
#include <TimerTC3.h>
#include <LiquidCrystal_PCF8574.h>



//u8x8_SSD1306_128X64_NONAME_HW_I2C //u8x8(/* reset=*/ //u8x8_PIN_NONE);
LiquidCrystal_PCF8574 lcd(0x27);
// //u8x8_SSD1306_128X64_NONAME_SW_I2C //u8x8(/* clock=*/ SCL, /* data=*/ SDA, /* reset=*/ //u8x8_PIN_NONE);   // OLEDs without Reset of the Display

// Define pins used
int left_gate_pin = 10;    // the number of the pin for left gate
int right_gate_pin = 11;  // number of pin for right gate
int i = 0;
int ledPin[2] =  {5, 6}; //LEFT, RIGHT
int ledState[2] = {LOW, LOW};
#define speakerPin A3
int interupt_test_pin = 12;

int debounce = 50;
bool pullup = true;
bool invert = true;
int gate_high_delay = 200;
int presses_init = 2;
int timeout = 2000;
int duration = 2000;
#define VBATPIN A7
#define sound_length 28
#define screen_period 800
#define display_wait 200
unsigned long  battery_wait = 10000;
#define run_end_delay 3000
#define led_interval 250 //time to leave the interval 
unsigned long inital_reset_delay = 2500; //in 100 seconds so 6000 = 60 seconds 2500 = 25 seconds
unsigned long reset_delay = 2500;


// Variables user in timng will change:
uint8_t presses = presses_init;
unsigned long time_now = 0;
unsigned long time_now_screen = 0;
unsigned long time_now_battery = 0;
unsigned long start_time[11];
unsigned long stop_time[11];
unsigned long last_stop_time = 0;
unsigned long last_start_time = 0;
unsigned long reset_start;
unsigned long reset_stop;
unsigned long last_display_time;
int n_start_time = 0;
int n_stop_time = 0;
unsigned long run_time;
int run_time_seconds;
int run_time_fraction;
bool run_once = false;
bool run_once_time_out = false;
//Control the backlight
unsigned long batt_last_read = 12000;
unsigned long back_light_on = 0;
bool debug = false;


//Menu status
int MenuId = 0;


unsigned long previousMillis [3] = {0, 0, 0};
unsigned long currentMillis [3] = {0, 0, 0};


EasyButton left_gate(left_gate_pin, debounce, pullup, invert);
EasyButton right_gate(right_gate_pin, debounce, pullup, invert);

FlashStorage(presses_storage, int);
FlashStorage(reset_delay_storage, unsigned long);
void setup() {
  if (debug){
  while (! Serial); }
  if (Serial) Serial.begin(9600);
  if (Serial) Serial.println(F("Starting New Version...."));
  Serial.setTimeout(100000);
  tone(A3, 600, 200);
  // initialize the LED pin as an output:
  left_gate.begin();
  right_gate.begin();
  //u8x8.begin();
  //u8x8.setFlipMode(1);   // set number from 1 to 3, the screen word will rotary 180
  //u8x8.setFont(//u8x8_font_chroma48medium8_r);
  //u8x8.setCursor(0, 0);
  //u8x8.clearDisplay();
  //u8x8.println("Ready");
  lcd.begin(20, 4); // initialize the lcd
  lcd.setBacklight(125); //turn on backlight

  lcd.home(); lcd.clear();
  lcd.setCursor(0, 0);

  lcd.print("Ready");
  //lcd.print(10);
  pinMode(speakerPin, OUTPUT);
  pinMode(LED_BUILTIN, OUTPUT);
  // set the digital pin as output:
  pinMode(ledPin[0], OUTPUT);
  pinMode(ledPin[1], OUTPUT);
  //pinMode(ledPin[2], OUTPUT);
  tone(A3, 600, 200);
  pinMode(interupt_test_pin, OUTPUT);
  pinMode(left_gate_pin, INPUT_PULLUP);
  pinMode(right_gate_pin, INPUT_PULLUP);
  //pinMode(back_light_enable, INPUT_PULLUP);
  //digitalWrite(bat_read_pin, HIGH);

  //get setting stored in flash ram
  reset_delay = reset_delay_storage.read();
  if (reset_delay == 0)reset_delay = inital_reset_delay;
  lcd.setCursor(0, 1);
  lcd.print("Run delay: "); lcd.print(reset_delay); lcd.print("msec");

  presses = presses_storage.read();
  if (presses == 0) presses = presses_init;
  lcd.setCursor(0, 2);
  lcd.print("Trigger pulses: "); lcd.print(presses);
  // Add the callback function to be called when the button is pressed for at least the given time.
  left_gate.onSequence(presses, timeout, left_gate_triggered);
  right_gate.onSequence(presses, timeout, right_gate_triggered);
  delay(2000);
  lcd.clear();
  lcd.setCursor(0, 0);
  lcd.print("Ready");


// user a timer interup to update the gates every 100 mseconds
//TimerTc3.initialize(100000);
//TimerTc3.attachInterrupt(read_gates);
}

void loop() {
  time_now = millis();
  read_gates();
  //if (Serial) Serial.println(start_time[0]);
  //if (Serial) Serial.println(n_start_time);
  //if (Serial) Serial.println(time_now);

  // IDisplay the time every second following the start of the run from the right
  if (n_stop_time > 0 && n_start_time == 0 && (time_now > last_display_time + display_wait))
  {
    run_from_right();
  }
  //function checks for a run from the left gate and stores the data
  if (n_start_time > 0 && n_stop_time == 0 && (time_now > last_display_time + display_wait))
  {
    run_from_left();
  }
  // Once we have a start time and a stop time diplay the run time
  if (n_stop_time > 0 && n_start_time > 0  && run_once == false)
  {
    display_run_time();
  }
  //
  //resent the counters ready for the next run
  if (n_stop_time > 0 && n_start_time > 0 && (time_now > last_display_time + run_end_delay))
  {
    reset_gates();
  }
  //If start but no 40 seconds passed then reset the counters.
  if (run_time > reset_delay && run_once_time_out == false) {
    time_out_reset();
  }
  turn_off_leds();
  if (Serial) MenuId = menu(); // call menu and display status = 0 sucess
  // read the state of the pushbutton value:
  battery_read(); //read and diaplay the battery voltage
}

void left_gate_triggered() //call back from easy button
{
  //Serial.println("left Gate Triggered");
  digitalWrite(LED_BUILTIN, HIGH);
  ////u8x8.setCursor(0, 3);
  ////u8x8.print("Left");;
  //tone(speakerPin, frequency,led_interval);
  tone(A3, 600, 200);
  start_time[n_start_time] = millis();
  ledState[0] = (HIGH);
  digitalWrite(ledPin[0], ledState[0]);
  previousMillis[0] = millis();
  lcd.setBacklight(125); //turn on back light
  back_light_on = millis();
  //if (Serial) Serial.println(n_start_time); if (Serial) Serial.print(start_time[n_start_time]);

  if (n_start_time < 9)
    n_start_time = n_start_time + 1;
  else n_start_time = 9;
}

void right_gate_triggered() //call back from easy button
{
  //Serial.println("Right Gate Triggered");
  digitalWrite(LED_BUILTIN, HIGH);
  ////u8x8.setCursor(6, 3);
  ////u8x8.print("Right");;
  //tone(speakerPin, frequency,led_interval);
  //tone(ledPin[2], frequency,led_interval);
  tone(A3, 440, 200);
  stop_time[n_stop_time] = millis();
  ledState[1] = (HIGH);
  digitalWrite(ledPin[1], ledState[1]);
  previousMillis[1] = millis();
  lcd.setBacklight(125); //turn on back light
  back_light_on = millis();
  //if (Serial) Serial.println(n_stop_time);
  //if (Serial) Serial.println(stop_time[n_stop_time]);
  if (n_stop_time < 9)
    n_stop_time = n_stop_time + 1;
  else n_stop_time = 9;
}


void read_gates()
{
  digitalWrite(interupt_test_pin, HIGH);
  left_gate.read();
  right_gate.read();
  
}

void run_from_left()
//function checks for a run from the left gate and stores the data
{
  time_now = millis();
  //if (Serial) Serial.println(start_time[0]);
  run_time = (time_now - start_time[0]) / 10;
  run_time_seconds = run_time / 100;
  run_time_fraction = run_time - (run_time_seconds * 100);
  //if (Serial) Serial.println(F("Run Time from Left...."));
  //if (Serial) Serial.print(run_time_seconds);
  //if (Serial) Serial.print(".");
  //if (Serial) Serial.println(run_time_fraction);
  lcd.setCursor(0, 0);
  lcd.print("Running from left...");
  lcd.setCursor(0, 1);
  lcd.print(run_time_seconds);
  lcd.print(".");
  lcd.print(run_time_fraction);
  lcd.print("  ");
  //u8x8.clearLine(0);
  //u8x8.setCursor(0, 0);
  //u8x8.print("Run from left");
  //u8x8.clearLine(1);
  //u8x8.clearLine(2);
  //u8x8.setCursor(0, 1);
  //u8x8.print(run_time_seconds);
  //u8x8.print(".");
  //u8x8.print(run_time_fraction);
  //u8x8.print("  ");
  last_display_time = time_now;
  run_once_time_out = false;
}

void run_from_right()
{
  time_now = millis();
  //if (Serial) Serial.println(start_time[0]);
  run_time = (time_now - stop_time[0]) / 10;
  run_time_seconds = run_time / 100;
  run_time_fraction = run_time - (run_time_seconds * 100);
  //if (Serial) Serial.println(F("Run Time from Right"));
  //if (Serial) Serial.print(run_time_seconds);
  //if (Serial) Serial.print(".");
  //if (Serial) Serial.println(run_time_fraction);
  lcd.setCursor(0, 0);
  lcd.print("Running from right..");
  lcd.setCursor(0, 1);
  lcd.print(run_time_seconds);
  lcd.print(".");
  lcd.print(run_time_fraction);
  lcd.print("  ");
  //u8x8.clearLine(0);
  //u8x8.setCursor(0, 0);
  //u8x8.print("Run from right");
  //u8x8.clearLine(1);
  //u8x8.clearLine(2);
  //u8x8.setCursor(0, 1);
  //u8x8.print(run_time_seconds);
  //u8x8.print(".");
  //u8x8.print(run_time_fraction);
  //u8x8.print("  ");
  last_display_time = time_now;
  run_once_time_out = false;
}


void display_run_time()
{
  // calculate and display the result
  //if (Serial) Serial.println(F("Start time...."));
  //if (Serial) Serial.println(start_time[0]);
  //if (Serial) Serial.println(F("Stop time...."));
  //if (Serial) Serial.println(stop_time[0]);
  if (stop_time[0] > start_time[0])
  {
    run_time = (stop_time[0] - start_time[0]) / 10;
  }
  else
  {
    run_time = (start_time[0] - stop_time[0]) / 10;
  }
  run_time_seconds = run_time / 100;
  run_time_fraction = run_time - (run_time_seconds * 100);
  if (Serial) Serial.print(F("Run Time: "));
  //u8x8.setCursor(0, 0);
  //u8x8.clearLine(0);
  //u8x8.print("Run Time");
  if (Serial) Serial.print(run_time_seconds);
  if (Serial) Serial.print(".");
  if (Serial) Serial.println(run_time_fraction);
  //u8x8.clearLine(1);
  //u8x8.setCursor(0, 1);
  //u8x8.print(run_time_seconds);
  //u8x8.print(".");
  //u8x8.print(run_time_fraction);
  //u8x8.print(" ");

  lcd.setCursor(0, 0);
  lcd.print("Run Time            "); lcd.setCursor(0, 1);
  lcd.print(run_time_seconds);
  lcd.print(".");
  lcd.print(run_time_fraction);
  lcd.print(" ");
  run_once = true;
}

void reset_gates() {
  n_stop_time = 0;
  n_start_time = 0;
  run_once = false;
  tone(A3, 350, 400);
  previousMillis[2] = millis();
  ledState[0] = (HIGH);
  digitalWrite(ledPin[0], ledState[0]);
  previousMillis[0] = millis();
  ledState[1] = (HIGH);
  digitalWrite(ledPin[1], ledState[1]);
  digitalWrite(LED_BUILTIN, LOW);
  previousMillis[1] = millis();
  lcd.setCursor(0, 0);
  lcd.print("Ready For Next Run");
  lcd.setBacklight(125); //turn on back light
  back_light_on = millis();
  //u8x8.setCursor(0, 0);
  //u8x8.clearLine(0);
  //u8x8.print("Ready For Next");
}

void time_out_reset()
{
  //if (Serial) Serial.println(start_time[0]);
  //if (Serial) Serial.println(F("Time Out Reset........."));
  lcd.setCursor(0, 0);
  lcd.print("Time Out Reset......");
  //u8x8.clearLine(0);
  //u8x8.setCursor(0, 0);
  //u8x8.print("Time Out Reset");
  n_stop_time = 0;
  n_start_time = 0;
  run_once_time_out = true;
  tone(A3, 350, 800);
  previousMillis[2] = millis();
  ledState[0] = (HIGH);
  digitalWrite(ledPin[0], ledState[0]);
  previousMillis[0] = millis();
  ledState[1] = (HIGH);
  digitalWrite(ledPin[1], ledState[1]);
  previousMillis[1] = millis();
  lcd.setBacklight(125); //turn on back light
  back_light_on = millis();
}
void turn_off_leds()
{
  // Turns off the status LEDs and the Buzzer after a wait time.
  for (i = 0; i <= 1; i++) {
    currentMillis [i] = millis();
    if (currentMillis[i] - previousMillis[i] >= led_interval) {
      // save the last time you blinked the LED
      // if the LED is off turn it on and vice-versa:
      if (ledState [i] == LOW) {
        ledState [i] = LOW;
      } else {
        ledState [i] = LOW;
      }
      // set the LED with the ledState of the variable:
      digitalWrite(ledPin[i], ledState[i]);
    }
  }
  if (millis() > time_now_screen + screen_period) {
    time_now_screen = millis();
    //u8x8.clearLine(5);
  }
}

void battery_read()
{
  if (millis() > (time_now_battery +  battery_wait ))
  {
    time_now_battery = millis();
    int measuredvbat = analogRead(VBATPIN);
    //measuredvbat *= 2;    // we divided by 2, so multiply back
    //measuredvbat *= 3.3;  // Multiply by 3.3V, our reference voltage minimun 2 volts
    //measuredvbat /= 1024; // convert to voltage
    // 155 per volt vmin (3.2v) = 496 vmax (4.2v) = 651.
    // Battry Charge = 100*(measuredvbat - vmin) / (vmax-vmin) = (measuredvbat - 496)/ 155
    //  max 100*(651 - 496) / 155 = 100
    // 100 (496 - 496) / 155 =0
    measuredvbat = 100 * (measuredvbat - 496) / 155;
    lcd.setCursor(0, 3);
    lcd.print("VBat: " ); lcd.print(measuredvbat); lcd.print("%" );
  }
}

int menu() {
  int menuId = 0;
  if (Serial.available() > 0 ) {
    switch (Serial.read())
    {
      case '1':
        flushRx();
        settings();
        menuId = 1;
        break;

      case '2':
        flushRx();
        readAndStorePresses();
        menuId = 2;
        break;

      case '3':
        flushRx();
        readAndStoreRunTimeout();
        menuId = 3;
        break;

      default:
        flushRx();
        Serial.println();
        Serial.println("Timing gate Control Menu");
        Serial.println("-------------------------------------");
        Serial.println("1) Display Setting");
        Serial.println("2) Change number of triggers to set of gate");
        Serial.println("3) Change run timeout");
        menuId = 0;
        break;
    }
  }
  return menuId;
}
void settings() {
  Serial.println();
  Serial.println("Settings");
  Serial.println("-------------------------------------");
  Serial.print("Number of triggers (legs) to set off gate: "); Serial.println(presses);
  int timeout_sec = timeout / 1000;
  Serial.print("Time out delay for start or end gate     : "); Serial.print(timeout_sec); Serial.println(" sec");
  int reset_delay_sec = reset_delay / 100;
  Serial.print("Time out to reset run                    : "); Serial.print(reset_delay_sec); Serial.println(" sec");
}
void readAndStorePresses()
{ uint8_t new_presses = 0;
  Serial.println("Please number of presses required between 1-5:");
  do {
    if (Serial.available() > 0) {
      String new_presses_string = Serial.readStringUntil('\n');
      new_presses = new_presses_string.toInt();
    }
  } while (new_presses == 0);
  presses_storage.write(new_presses);  // <-- save the new number of presses
  presses = new_presses;
  Serial.print("New presses: "); Serial.print(presses); Serial.println(" reset to activate");
}

void readAndStoreRunTimeout()
{ uint8_t new_run_timeout = 0;
  Serial.println("Please maximum expected run time before reset (90 m track = 25 Polish = 120");
  do {
    if (Serial.available() > 0) {
      String new_run_timeout_string = Serial.readStringUntil('\n');
      new_run_timeout = new_run_timeout_string.toInt();
    }
  } while (new_run_timeout == 0);
  reset_delay = new_run_timeout * 100;
  reset_delay_storage.write(reset_delay);  // <-- save the new number of presses
  Serial.print("New reset: "); Serial.print(new_run_timeout); Serial.println(" reset to activate");
}

void flushRx() {
  while (Serial.available()) {
    Serial.read();
    delay(1);
  }
}
